// Logisim project memory_game_final.circ as structural Verilog: 14 circuits, main circuit main
module main (
);

  wire b0, b1, b2, b3, b4, b5, b6, b7, b8, b9, Check, correct, ep, game_end, lose, miss, Mode, ModeButton,
       not_1_out, Play, Reset, SoundButton, SoundsON, TimeOut, win;
  wire [3:0] m0, m1, points, s0, s1, tries;
  wire [4:0] single_display_1_out_7, single_display_1_out_8, single_display_1_out_9, single_display_1_out_10,
       single_display_1_out_11, single_display_2_out_7, single_display_2_out_8, single_display_2_out_9,
       single_display_2_out_10, single_display_2_out_11, single_display_3_out_7, single_display_3_out_8,
       single_display_3_out_9, single_display_3_out_10, single_display_3_out_11, single_display_4_out_7,
       single_display_4_out_8, single_display_4_out_9, single_display_4_out_10, single_display_4_out_11,
       single_display_5_out_7, single_display_5_out_8, single_display_5_out_9, single_display_5_out_10,
       single_display_5_out_11, single_display_mirrored_1_out_7, single_display_mirrored_1_out_8,
       single_display_mirrored_1_out_9, single_display_mirrored_1_out_10, single_display_mirrored_1_out_11,
       single_display_mirrored_2_out_7, single_display_mirrored_2_out_8, single_display_mirrored_2_out_9,
       single_display_mirrored_2_out_10, single_display_mirrored_2_out_11, single_display_mirrored_3_out_7,
       single_display_mirrored_3_out_8, single_display_mirrored_3_out_9, single_display_mirrored_3_out_10,
       single_display_mirrored_3_out_11, single_display_mirrored_4_out_7, single_display_mirrored_4_out_8,
       single_display_mirrored_4_out_9, single_display_mirrored_4_out_10, single_display_mirrored_4_out_11,
       single_display_mirrored_5_out_7, single_display_mirrored_5_out_8, single_display_mirrored_5_out_9,
       single_display_mirrored_5_out_10, single_display_mirrored_5_out_11;
  wire [24:0] d0, d1, d2, d3, d4, d5, d6, d7, d8, d9;

  Button button_1 (.out(Reset));
  Button button_2 (.out(Play));
  Button button_3 (.out(SoundButton));
  LED led_1 (.in(SoundsON));
  Button button_4 (.out(ModeButton));
  LED led_2 (.in(Mode));
  not not_1 (not_1_out, Mode);
  LED led_3 (.in(not_1_out));
  Hex_Digit_Display hex_digit_display_1 (.value(tries));  // open: dp
  Button button_5 (.out(Check));
  single_display single_display_1 (
    .d(d0), .b(b0), .ep(ep), .miss(miss), .correct(correct), .in_6(Reset), .out_7(single_display_1_out_7),
    .out_8(single_display_1_out_8), .out_9(single_display_1_out_9), .out_10(single_display_1_out_10),
    .out_11(single_display_1_out_11));
  DotMatrix #(.matrixrows(5)) dotmatrix_1 (
    .col0(single_display_1_out_11), .col1(single_display_1_out_10), .col2(single_display_1_out_9),
    .col3(single_display_1_out_8), .col4(single_display_1_out_7));
  DotMatrix #(.matrixrows(5)) dotmatrix_2 (
    .col0(single_display_2_out_11), .col1(single_display_2_out_10), .col2(single_display_2_out_9),
    .col3(single_display_2_out_8), .col4(single_display_2_out_7));
  DotMatrix #(.matrixrows(5)) dotmatrix_3 (
    .col0(single_display_mirrored_1_out_7), .col1(single_display_mirrored_1_out_8),
    .col2(single_display_mirrored_1_out_9), .col3(single_display_mirrored_1_out_10),
    .col4(single_display_mirrored_1_out_11));
  DotMatrix #(.matrixrows(5)) dotmatrix_4 (
    .col0(single_display_mirrored_2_out_7), .col1(single_display_mirrored_2_out_8),
    .col2(single_display_mirrored_2_out_9), .col3(single_display_mirrored_2_out_10),
    .col4(single_display_mirrored_2_out_11));
  single_display_mirrored single_display_mirrored_1 (
    .in_1(d1), .in_2(b1), .in_3(ep), .in_4(miss), .correct(correct), .in_6(Reset),
    .out_7(single_display_mirrored_1_out_7), .out_8(single_display_mirrored_1_out_8),
    .out_9(single_display_mirrored_1_out_9), .out_10(single_display_mirrored_1_out_10),
    .out_11(single_display_mirrored_1_out_11));
  single_display_mirrored single_display_mirrored_2 (
    .in_1(d3), .in_2(b3), .in_3(ep), .in_4(miss), .correct(correct), .in_6(Reset),
    .out_7(single_display_mirrored_2_out_7), .out_8(single_display_mirrored_2_out_8),
    .out_9(single_display_mirrored_2_out_9), .out_10(single_display_mirrored_2_out_10),
    .out_11(single_display_mirrored_2_out_11));
  Button button_6 (.out(b0));
  Button button_7 (.out(b1));
  T_Flip_Flop t_ff_1 (.T(SoundButton), .clk(SoundButton), .Qn(SoundsON));  // open: Q, reset, preset
  T_Flip_Flop t_ff_2 (.T(ModeButton), .clk(ModeButton), .Qn(Mode));  // open: Q, reset, preset
  Hex_Digit_Display hex_digit_display_2 (.value(points));  // open: dp
  single_display single_display_2 (
    .d(d2), .b(b2), .ep(ep), .miss(miss), .correct(correct), .in_6(Reset), .out_7(single_display_2_out_7),
    .out_8(single_display_2_out_8), .out_9(single_display_2_out_9), .out_10(single_display_2_out_10),
    .out_11(single_display_2_out_11));
  DotMatrix #(.matrixrows(5)) dotmatrix_5 (
    .col0(single_display_3_out_11), .col1(single_display_3_out_10), .col2(single_display_3_out_9),
    .col3(single_display_3_out_8), .col4(single_display_3_out_7));
  DotMatrix #(.matrixrows(5)) dotmatrix_6 (
    .col0(single_display_mirrored_3_out_7), .col1(single_display_mirrored_3_out_8),
    .col2(single_display_mirrored_3_out_9), .col3(single_display_mirrored_3_out_10),
    .col4(single_display_mirrored_3_out_11));
  single_display_mirrored single_display_mirrored_3 (
    .in_1(d5), .in_2(b5), .in_3(ep), .in_4(miss), .correct(correct), .in_6(Reset),
    .out_7(single_display_mirrored_3_out_7), .out_8(single_display_mirrored_3_out_8),
    .out_9(single_display_mirrored_3_out_9), .out_10(single_display_mirrored_3_out_10),
    .out_11(single_display_mirrored_3_out_11));
  Button button_8 (.out(b2));
  Button button_9 (.out(b4));
  Button button_10 (.out(b3));
  Button button_11 (.out(b5));
  single_display single_display_3 (
    .d(d4), .b(b4), .ep(ep), .miss(miss), .correct(correct), .in_6(Reset), .out_7(single_display_3_out_7),
    .out_8(single_display_3_out_8), .out_9(single_display_3_out_9), .out_10(single_display_3_out_10),
    .out_11(single_display_3_out_11));
  single_display single_display_4 (
    .d(d6), .b(b6), .ep(ep), .miss(miss), .correct(correct), .in_6(Reset), .out_7(single_display_4_out_7),
    .out_8(single_display_4_out_8), .out_9(single_display_4_out_9), .out_10(single_display_4_out_10),
    .out_11(single_display_4_out_11));
  DotMatrix #(.matrixrows(5)) dotmatrix_7 (
    .col0(single_display_4_out_11), .col1(single_display_4_out_10), .col2(single_display_4_out_9),
    .col3(single_display_4_out_8), .col4(single_display_4_out_7));
  DotMatrix #(.matrixrows(5)) dotmatrix_8 (
    .col0(single_display_mirrored_4_out_7), .col1(single_display_mirrored_4_out_8),
    .col2(single_display_mirrored_4_out_9), .col3(single_display_mirrored_4_out_10),
    .col4(single_display_mirrored_4_out_11));
  single_display_mirrored single_display_mirrored_4 (
    .in_1(d7), .in_2(b7), .in_3(ep), .in_4(miss), .correct(correct), .in_6(Reset),
    .out_7(single_display_mirrored_4_out_7), .out_8(single_display_mirrored_4_out_8),
    .out_9(single_display_mirrored_4_out_9), .out_10(single_display_mirrored_4_out_10),
    .out_11(single_display_mirrored_4_out_11));
  Button button_12 (.out(b6));
  Button button_13 (.out(b8));
  Button button_14 (.out(b7));
  Button button_15 (.out(b9));
  Hex_Digit_Display hex_digit_display_3 (.value(m1));  // open: dp
  Hex_Digit_Display hex_digit_display_4 (.value(m0));  // open: dp
  single_display single_display_5 (
    .d(d8), .b(b8), .ep(ep), .miss(miss), .correct(correct), .in_6(Reset), .out_7(single_display_5_out_7),
    .out_8(single_display_5_out_8), .out_9(single_display_5_out_9), .out_10(single_display_5_out_10),
    .out_11(single_display_5_out_11));
  DotMatrix #(.matrixrows(5)) dotmatrix_9 (
    .col0(single_display_5_out_11), .col1(single_display_5_out_10), .col2(single_display_5_out_9),
    .col3(single_display_5_out_8), .col4(single_display_5_out_7));
  DotMatrix #(.matrixrows(5)) dotmatrix_10 (
    .col0(single_display_mirrored_5_out_7), .col1(single_display_mirrored_5_out_8),
    .col2(single_display_mirrored_5_out_9), .col3(single_display_mirrored_5_out_10),
    .col4(single_display_mirrored_5_out_11));
  single_display_mirrored single_display_mirrored_5 (
    .in_1(d9), .in_2(b9), .in_3(ep), .in_4(miss), .correct(correct), .in_6(Reset),
    .out_7(single_display_mirrored_5_out_7), .out_8(single_display_mirrored_5_out_8),
    .out_9(single_display_mirrored_5_out_9), .out_10(single_display_mirrored_5_out_10),
    .out_11(single_display_mirrored_5_out_11));
  DotMatrix #(.matrixcols(1), .matrixrows(1)) dotmatrix_11 ();  // open: col0
  DotMatrix #(.matrixcols(1), .matrixrows(1)) dotmatrix_12 ();  // open: col0
  Hex_Digit_Display hex_digit_display_5 (.value(s1));  // open: dp
  LED led_4 (.in(win));
  LED led_5 (.in(lose));
  Hex_Digit_Display hex_digit_display_6 (.value(s0));  // open: dp
  SoundSystem soundsystem_1 (.Reset(Reset), .SoundsON(SoundsON), .Match(correct), .Wrong(miss), .Win(win), .Lose(lose));
  Clock clock_1 ();  // open: out
  screen screen_1 (
    .in_1(Play), .in_2(Reset), .win(win), .lose(lose), .d0(d0), .d1(d1), .d2(d2), .d3(d3), .d4(d4), .d5(d5),
    .d6(d6), .d7(d7), .d8(d8), .d9(d9), .placing_done(ep));
  buttons buttons_1 (
    .check(Check), .b0(b0), .b1(b1), .b2(b2), .b3(b3), .b4(b4), .b5(b5), .b6(b6), .b7(b7), .b8(b8), .b9(b9),
    .in_12(d0), .in_13(d1), .in_14(d2), .in_15(d3), .in_16(d4), .in_17(d5), .in_18(d6), .in_19(d7),
    .in_20(d8), .in_21(d9), .correct(correct), .wrong(miss));
  timer timer_1 (.set(Play), .reset(Reset), .in_3(game_end), .TimeOut(TimeOut), .t3(m1), .t2(m0), .t1(s1), .t0(s0));
  score score_1 (
    .timeOut(TimeOut), .mode(Mode), .correct(correct), .wrong(miss), .reset(Reset), .win(win),
    .points(points), .lose(lose), .tries(tries));
  or or_1 (game_end, win, lose);

  // Notes on the sheet:
  //   HardMode
  //   EasyMode
endmodule

module screen (
  input  in_1,
  input  in_2,
  input  win,
  input  lose,
  output [24:0] d0,
  output [24:0] d1,
  output [24:0] d2,
  output [24:0] d3,
  output [24:0] d4,
  output [24:0] d5,
  output [24:0] d6,
  output [24:0] d7,
  output [24:0] d8,
  output [24:0] d9,
  output placing_done
);

  wire and_1_out, and_3_out, and_4_out, and_5_out, and_6_out, and_7_out, and_9_out, and_10_out, and_11_out,
       and_12_out, and_13_out, clk, doCount, end_b, eq0, eq1, eq2, eq3, eq4, eq5, eq6, eq7, eq8, eq9,
       game_end, n0, n1, n2, n3, n4, n5, n6, n7, n8, n9, not_1_out, not_2_out, not_3_out, not_4_out,
       not_5_out, not_6_out, not_7_out, not_8_out, not_9_out, not_10_out, not_11_out, not_12_out, or_2_out,
       r0, r1, r2, r3, r4, r5, r6, r7, r8, r9, start;
  wire [1:0] priority_encoder_1_out, priority_encoder_2_out, priority_encoder_3_out, priority_encoder_4_out,
       priority_encoder_5_out, priority_encoder_6_out, priority_encoder_7_out, priority_encoder_8_out,
       priority_encoder_9_out, priority_encoder_10_out;
  wire [3:0] count, randN;
  wire [24:0] c0, c1, c2, c3, c4, d0_t, d1_t, d2_t, d3_t, d4_t, d5_t, d6_t, d7_t, d8_t, d9_t,
       multiplexer_1_out, multiplexer_2_out, multiplexer_3_out, multiplexer_4_out, multiplexer_5_out,
       multiplexer_6_out, multiplexer_7_out, multiplexer_8_out, multiplexer_9_out, multiplexer_10_out,
       multiplexer_11_out;

  Clock clock_1 (.out(clk));
  deck deck_1 (.in_1(in_1), .in_2(in_2), .out_3(c0), .out_4(c1), .out_5(c2), .out_6(c3), .out_7(c4), .out_8(end_b));
  Multiplexer #(.select(4), .width(25)) multiplexer_1 (
    .in0(c0), .in1(c0), .in2(c1), .in3(c1), .in4(c2), .in5(c2), .in6(c3), .in7(c3), .in8(c4), .in9(c4),
    .out(multiplexer_1_out), .sel(count));  // open: in10, in11, in12, in13, in14, in15
  not not_1 (not_1_out, game_end);
  not not_2 (not_2_out, game_end);
  not not_3 (not_3_out, game_end);
  not not_4 (not_4_out, game_end);
  not not_5 (not_5_out, game_end);
  Demultiplexer #(.select(4), .width(25)) demultiplexer_1 (
    .out0(d0_t), .out1(d1_t), .out2(d2_t), .out3(d3_t), .out4(d4_t), .out5(d5_t), .out6(d6_t), .out7(d7_t),
    .out8(d8_t), .out9(d9_t), .in(multiplexer_1_out), .sel(randN));  // open: out10, out11, out12, out13, out14, out15
  Priority_Encoder #(.select(2)) priority_encoder_1 (
    .in0(not_1_out), .in1(win), .in2(lose), .out(priority_encoder_1_out));  // open: in3, gs, en_out, en_in
  Priority_Encoder #(.select(2)) priority_encoder_2 (
    .in0(not_2_out), .in1(win), .in2(lose), .out(priority_encoder_2_out));  // open: in3, gs, en_out, en_in
  Priority_Encoder #(.select(2)) priority_encoder_3 (
    .in0(not_3_out), .in1(win), .in2(lose), .out(priority_encoder_3_out));  // open: in3, gs, en_out, en_in
  Priority_Encoder #(.select(2)) priority_encoder_4 (
    .in0(not_4_out), .in1(win), .in2(lose), .out(priority_encoder_4_out));  // open: in3, gs, en_out, en_in
  Priority_Encoder #(.select(2)) priority_encoder_5 (
    .in0(not_5_out), .in1(win), .in2(lose), .out(priority_encoder_5_out));  // open: in3, gs, en_out, en_in
  Multiplexer #(.select(2), .width(25)) multiplexer_2 (
    .in0(d0_t), .in1({25{1'b0}}), .in2(25'h1f8d6e0), .out(multiplexer_2_out), .sel(priority_encoder_1_out));  // open: in3
  Multiplexer #(.select(2), .width(25)) multiplexer_3 (
    .in0(d2_t), .in1(25'h1041d10), .in2(25'h1fa53e0), .out(multiplexer_3_out), .sel(priority_encoder_2_out));  // open: in3
  Multiplexer #(.select(2), .width(25)) multiplexer_4 (
    .in0(d4_t), .in1(25'h1f8c7e0), .in2(25'h1f4111f), .out(multiplexer_4_out), .sel(priority_encoder_3_out));  // open: in3
  Multiplexer #(.select(2), .width(25)) multiplexer_5 (
    .in0(d6_t), .in1(25'hf843f), .in2(25'hfd6b5), .out(multiplexer_5_out), .sel(priority_encoder_4_out));  // open: in3
  Multiplexer #(.select(2), .width(25)) multiplexer_6 (
    .in0(d8_t), .in1({25{1'b0}}), .in2({25{1'b0}}), .out(multiplexer_6_out), .sel(priority_encoder_5_out));  // open: in3
  and and_1 (and_1_out, start, not_6_out);
  not not_6 (not_6_out, game_end);
  or or_1 (game_end, win, lose);
  Register #(.width(25)) register_1 (.D(multiplexer_2_out), .en(r0), .clk(clk), .Q(d0), .clr(in_2));
  Register #(.width(25)) register_2 (.D(multiplexer_3_out), .en(r2), .clk(clk), .Q(d2), .clr(in_2));
  Register #(.width(25)) register_3 (.D(multiplexer_4_out), .en(r4), .clk(clk), .Q(d4), .clr(in_2));
  Register #(.width(25)) register_4 (.D(multiplexer_5_out), .en(r6), .clk(clk), .Q(d6), .clr(in_2));
  Register #(.width(25)) register_5 (.D(multiplexer_6_out), .en(r8), .clk(clk), .Q(d8), .clr(in_2));
  Random #(.width(4)) random_1 (.next(and_1_out), .clk(clk), .out(randN));  // open: clr
  not not_7 (not_7_out, game_end);
  not not_8 (not_8_out, game_end);
  not not_9 (not_9_out, game_end);
  not not_10 (not_10_out, game_end);
  not not_11 (not_11_out, game_end);
  or or_2 (or_2_out, eq0, eq1, eq2, eq3, eq4, eq5, eq6, eq7, eq8, eq9);
  Priority_Encoder #(.select(2)) priority_encoder_6 (
    .in0(not_7_out), .in1(win), .in2(lose), .out(priority_encoder_6_out));  // open: in3, gs, en_out, en_in
  Priority_Encoder #(.select(2)) priority_encoder_7 (
    .in0(not_8_out), .in1(win), .in2(lose), .out(priority_encoder_7_out));  // open: in3, gs, en_out, en_in
  Priority_Encoder #(.select(2)) priority_encoder_8 (
    .in0(not_9_out), .in1(win), .in2(lose), .out(priority_encoder_8_out));  // open: in3, gs, en_out, en_in
  Priority_Encoder #(.select(2)) priority_encoder_9 (
    .in0(not_10_out), .in1(win), .in2(lose), .out(priority_encoder_9_out));  // open: in3, gs, en_out, en_in
  Priority_Encoder #(.select(2)) priority_encoder_10 (
    .in0(not_11_out), .in1(win), .in2(lose), .out(priority_encoder_10_out));  // open: in3, gs, en_out, en_in
  Counter #(.max('ha), .width(4)) counter_1 (
    .clr(not_12_out), .count(doCount), .clk(clk), .Q(count));  // open: load, up, D, carry
  not not_12 (not_12_out, end_b);
  and and_2 (start, or_2_out, end_b);
  Register #(.width(25)) register_6 (.D(multiplexer_7_out), .en(r1), .clk(clk), .Q(d1), .clr(in_2));
  Multiplexer #(.select(2), .width(25)) multiplexer_7 (
    .in0(d1_t), .in1({25{1'b0}}), .in2(25'h1f8c7e0), .out(multiplexer_7_out), .sel(priority_encoder_6_out));  // open: in3
  Register #(.width(25)) register_7 (.D(multiplexer_8_out), .en(r3), .clk(clk), .Q(d3), .clr(in_2));
  Multiplexer #(.select(2), .width(25)) multiplexer_8 (
    .in0(d3_t), .in1(25'h1e1907e), .in2(25'h18304d8), .out(multiplexer_8_out), .sel(priority_encoder_7_out));  // open: in3
  Register #(.width(25)) register_8 (.D(multiplexer_9_out), .en(r5), .clk(clk), .Q(d5), .clr(in_2));
  Multiplexer #(.select(2), .width(25)) multiplexer_9 (
    .in0(d5_t), .in1(25'h8fe20), .in2(25'hfd6b5), .out(multiplexer_9_out), .sel(priority_encoder_8_out));  // open: in3
  Register #(.width(25)) register_9 (.D(multiplexer_10_out), .en(r7), .clk(clk), .Q(d7), .clr(in_2));
  Multiplexer #(.select(2), .width(25)) multiplexer_10 (
    .in0(d7_t), .in1(25'h1f4105f), .in2(25'hfd28b), .out(multiplexer_10_out), .sel(priority_encoder_9_out));  // open: in3
  Register #(.width(25)) register_10 (.D(multiplexer_11_out), .en(r9), .clk(clk), .Q(d9), .clr(in_2));
  Multiplexer #(.select(2), .width(25)) multiplexer_11 (
    .in0(d9_t), .in1({25{1'b0}}), .in2({25{1'b0}}), .out(multiplexer_11_out), .sel(priority_encoder_10_out));  // open: in3
  Demultiplexer #(.select(4)) demultiplexer_2 (
    .out0(n0), .out1(n1), .out2(n2), .out3(n3), .out4(n4), .out5(n5), .out6(n6), .out7(n7), .out8(n8),
    .out9(n9), .in(start), .sel(randN));  // open: out10, out11, out12, out13, out14, out15
  Comparator #(.width(25)) comparator_1 (.a(d0), .b({25{1'b0}}), .eq(eq0));  // open: gt, lt
  Comparator #(.width(25)) comparator_2 (.a(d2), .b({25{1'b0}}), .eq(eq2));  // open: gt, lt
  Comparator #(.width(25)) comparator_3 (.a(d4), .b({25{1'b0}}), .eq(eq4));  // open: gt, lt
  Comparator #(.width(25)) comparator_4 (.a(d6), .b({25{1'b0}}), .eq(eq6));  // open: gt, lt
  Comparator #(.width(25)) comparator_5 (.a(d8), .b({25{1'b0}}), .eq(eq8));  // open: gt, lt
  and and_3 (and_3_out, n0, eq0);
  and and_4 (and_4_out, n2, eq2);
  and and_5 (and_5_out, n4, eq4);
  and and_6 (and_6_out, n6, eq6);
  and and_7 (and_7_out, n8, eq8);
  Multiplexer #(.select(4)) multiplexer_12 (
    .in0(r0), .in1(r1), .in2(r2), .in3(r3), .in4(r4), .in5(r5), .in6(r6), .in7(r7), .in8(r8), .in9(r9),
    .in10(1'b0), .in11(1'b0), .in12(1'b0), .in13(1'b0), .in14(1'b0), .in15(1'b0), .out(doCount), .sel(randN));
  or or_3 (r0, game_end, and_3_out);
  or or_4 (r2, game_end, and_4_out);
  or or_5 (r4, game_end, and_5_out);
  or or_6 (r6, game_end, and_6_out);
  or or_7 (r8, game_end, and_7_out);
  and and_8 (placing_done, ~eq0, ~eq1, ~eq2, ~eq3, ~eq4, ~eq5, ~eq6, ~eq7, ~eq8, ~eq9);  // AND_Gate
  Comparator #(.width(25)) comparator_6 (.a(d1), .b({25{1'b0}}), .eq(eq1));  // open: gt, lt
  Comparator #(.width(25)) comparator_7 (.a(d3), .b({25{1'b0}}), .eq(eq3));  // open: gt, lt
  Comparator #(.width(25)) comparator_8 (.a(d5), .b({25{1'b0}}), .eq(eq5));  // open: gt, lt
  Comparator #(.width(25)) comparator_9 (.a(d7), .b({25{1'b0}}), .eq(eq7));  // open: gt, lt
  Comparator #(.width(25)) comparator_10 (.a(d9), .b({25{1'b0}}), .eq(eq9));  // open: gt, lt
  and and_9 (and_9_out, n1, eq1);
  and and_10 (and_10_out, n3, eq3);
  and and_11 (and_11_out, n5, eq5);
  and and_12 (and_12_out, n7, eq7);
  and and_13 (and_13_out, n9, eq9);
  or or_8 (r1, game_end, and_9_out);
  or or_9 (r3, game_end, and_10_out);
  or or_10 (r5, game_end, and_11_out);
  or or_11 (r7, game_end, and_12_out);
  or or_12 (r9, game_end, and_13_out);

  // Other names for the same wires on the sheet: q0[24:0] = d0; q1[24:0] = d1; q2[24:0] = d2; q3[24:0] = d3;
  //   q4[24:0] = d4; q5[24:0] = d5; q6[24:0] = d6; q7[24:0] = d7; q8[24:0] = d8; q9[24:0] = d9; reset = in_2;
  //   set = in_1
endmodule

module deck (
  input  in_1,
  input  in_2,
  output [24:0] out_3,
  output [24:0] out_4,
  output [24:0] out_5,
  output [24:0] out_6,
  output [24:0] out_7,
  output out_8
);

  wire clk, not_1_out, r0, r1, r2, r3, r4, s_r_ff_1_q, start;
  wire [2:0] count;
  wire [4:0] bit_extender_1_out, bit_extender_2_out, bit_extender_3_out, bit_extender_4_out,
       bit_extender_5_out, bit_extender_6_out, bit_extender_7_out, bit_extender_8_out, bit_extender_9_out,
       bit_extender_10_out, bit_extender_11_out, bit_extender_12_out, bit_extender_13_out,
       bit_extender_14_out, bit_extender_15_out;
  wire [8:0] c0, c1, c2, c3, c4, random_1_out, register_1_q, register_2_q, register_3_q, register_4_q,
       register_5_q;

  Clock clock_1 (.out(clk));
  Register #(.width(9)) register_1 (.D(c0), .en(r0), .clk(clk), .Q(register_1_q), .clr(in_2));
  Register #(.width(9)) register_2 (.D(c1), .en(r1), .clk(clk), .Q(register_2_q), .clr(in_2));
  assign bit_extender_1_out = {{2{1'b0}}, register_1_q[2:0]};  // Bit_Extender bit_extender_1
  assign bit_extender_2_out = {{2{1'b0}}, register_1_q[5:3]};  // Bit_Extender bit_extender_2
  assign bit_extender_3_out = {{2{1'b0}}, register_1_q[8:6]};  // Bit_Extender bit_extender_3
  assign bit_extender_4_out = {{2{1'b0}}, register_2_q[2:0]};  // Bit_Extender bit_extender_4
  assign bit_extender_5_out = {{2{1'b0}}, register_2_q[5:3]};  // Bit_Extender bit_extender_5
  assign bit_extender_6_out = {{2{1'b0}}, register_2_q[8:6]};  // Bit_Extender bit_extender_6
  Random #(.width(9)) random_1 (.next(not_1_out), .clk(clk), .out(random_1_out));  // open: clr
  not not_1 (not_1_out, out_8);
  Shifter #(.width(5)) shifter_1 (.in(bit_extender_1_out), .\dist (3'b001), .out(out_3[9:5]));
  Shifter #(.width(5)) shifter_2 (.in(bit_extender_2_out), .\dist (3'b001), .out(out_3[14:10]));
  Shifter #(.width(5)) shifter_3 (.in(bit_extender_3_out), .\dist (3'b001), .out(out_3[19:15]));
  Shifter #(.width(5)) shifter_4 (.in(bit_extender_4_out), .\dist (3'b001), .out(out_6[9:5]));
  Shifter #(.width(5)) shifter_5 (.in(bit_extender_5_out), .\dist (3'b001), .out(out_6[14:10]));
  Shifter #(.width(5)) shifter_6 (.in(bit_extender_6_out), .\dist (3'b001), .out(out_6[19:15]));
  Demultiplexer #(.select(3), .width(9)) demultiplexer_1 (
    .out0(c0), .out1(c1), .out2(c2), .out3(c3), .out4(c4), .in(random_1_out), .sel(count));  // open: out5, out6, out7
  Register #(.width(9)) register_3 (.D(c2), .en(r2), .clk(clk), .Q(register_3_q), .clr(in_2));
  Register #(.width(9)) register_4 (.D(c3), .en(r3), .clk(clk), .Q(register_4_q), .clr(in_2));
  Counter #(.max('h5), .width(3)) counter_1 (
    .clr(in_2), .count(start), .clk(clk), .carry(out_8), .Q(count));  // open: load, up, D
  assign bit_extender_7_out = {{2{1'b0}}, register_3_q[2:0]};  // Bit_Extender bit_extender_7
  Shifter #(.width(5)) shifter_7 (.in(bit_extender_7_out), .\dist (3'b001), .out(out_4[9:5]));
  assign bit_extender_8_out = {{2{1'b0}}, register_3_q[5:3]};  // Bit_Extender bit_extender_8
  Shifter #(.width(5)) shifter_8 (.in(bit_extender_8_out), .\dist (3'b001), .out(out_4[14:10]));
  assign bit_extender_9_out = {{2{1'b0}}, register_3_q[8:6]};  // Bit_Extender bit_extender_9
  Shifter #(.width(5)) shifter_9 (.in(bit_extender_9_out), .\dist (3'b001), .out(out_4[19:15]));
  assign bit_extender_10_out = {{2{1'b0}}, register_4_q[2:0]};  // Bit_Extender bit_extender_10
  Shifter #(.width(5)) shifter_10 (.in(bit_extender_10_out), .\dist (3'b001), .out(out_7[9:5]));
  assign bit_extender_11_out = {{2{1'b0}}, register_4_q[5:3]};  // Bit_Extender bit_extender_11
  Shifter #(.width(5)) shifter_11 (.in(bit_extender_11_out), .\dist (3'b001), .out(out_7[14:10]));
  assign bit_extender_12_out = {{2{1'b0}}, register_4_q[8:6]};  // Bit_Extender bit_extender_12
  Shifter #(.width(5)) shifter_12 (.in(bit_extender_12_out), .\dist (3'b001), .out(out_7[19:15]));
  Decoder #(.select(3)) decoder_1 (
    .out0(r0), .out1(r1), .out2(r2), .out3(r3), .out4(r4), .sel(count));  // open: out5, out6, out7, en
  Register #(.width(9)) register_5 (.D(c4), .en(r4), .clk(clk), .Q(register_5_q), .clr(in_2));
  S_R_Flip_Flop s_r_ff_1 (.S(in_1), .R(in_2), .clk(clk), .Q(s_r_ff_1_q));  // open: reset, Qn, preset
  assign bit_extender_13_out = {{2{1'b0}}, register_5_q[2:0]};  // Bit_Extender bit_extender_13
  Shifter #(.width(5)) shifter_13 (.in(bit_extender_13_out), .\dist (3'b001), .out(out_5[9:5]));
  assign bit_extender_14_out = {{2{1'b0}}, register_5_q[5:3]};  // Bit_Extender bit_extender_14
  Shifter #(.width(5)) shifter_14 (.in(bit_extender_14_out), .\dist (3'b001), .out(out_5[14:10]));
  assign bit_extender_15_out = {{2{1'b0}}, register_5_q[8:6]};  // Bit_Extender bit_extender_15
  Shifter #(.width(5)) shifter_15 (.in(bit_extender_15_out), .\dist (3'b001), .out(out_5[19:15]));
  and and_1 (start, s_r_ff_1_q, ~out_8);  // AND_Gate

  assign {out_3[24:20], out_3[4:0]} = {10{1'b0}};
  assign {out_4[24:20], out_4[4:0]} = {10{1'b0}};
  assign {out_5[24:20], out_5[4:0]} = {10{1'b0}};
  assign {out_6[24:20], out_6[4:0]} = {10{1'b0}};
  assign {out_7[24:20], out_7[4:0]} = {10{1'b0}};

  // Other names for the same wires on the sheet: reset = in_2; set = in_1; stop = out_8
endmodule

// sc
module score (
  input  timeOut,
  input  mode,
  input  correct,
  input  wrong,
  input  reset,
  output win,
  output [3:0] points,
  output lose,
  output [3:0] tries
);

  wire and_1_out, and_2_out, and_3_out, counter_2_carry, or_1_out;
  wire [3:0] multiplexer_1_out;

  and and_1 (and_1_out, correct, ~wrong);  // AND_Gate
  and and_2 (and_2_out, wrong, ~correct);  // AND_Gate
  Multiplexer #(.width(4)) multiplexer_1 (.in0(4'b0011), .in1(4'b0001), .out(multiplexer_1_out), .sel(mode));
  Counter #(.max('h5), .ongoal("stay"), .width(4)) counter_1 (
    .clr(reset), .count(1'b1), .clk(and_1_out), .D(4'b0000), .carry(win), .Q(points));  // open: load, up
  Counter #(.max('h3), .ongoal("stay"), .width(4)) counter_2 (
    .load(reset), .up(1'b0), .clk(or_1_out), .D(multiplexer_1_out), .carry(counter_2_carry), .Q(tries));  // open: clr, count
  or or_1 (or_1_out, reset, and_2_out);
  and and_3 (and_3_out, timeOut, mode);
  or or_2 (lose, and_3_out, counter_2_carry);
endmodule

module timer (
  input  set,
  input  reset,
  input  in_3,
  output TimeOut,
  output [3:0] t3,
  output [3:0] t2,
  output [3:0] t1,
  output [3:0] t0
);

  wire a_min, a_sec, h, min, or_1_out, or_2_out, or_3_out;

  or or_1 (or_1_out, min, reset);
  or or_2 (or_2_out, h, reset);
  seconds_counter seconds_counter_1 (.game_end(in_3), .reset(reset), .set(set), .asec(a_sec), .s(t0));
  Counter #(.max('h5), .width(4)) counter_1 (
    .clr(or_1_out), .clk(a_sec), .carry(min), .Q(t1));  // open: load, up, count, D
  Counter #(.max('h9), .width(4)) counter_2 (
    .clr(or_2_out), .clk(a_min), .carry(h), .Q(t3));  // open: load, up, count, D
  or or_3 (or_3_out, a_min, reset);
  Counter #(.max('h9), .width(4)) counter_3 (
    .clr(or_3_out), .clk(min), .carry(a_min), .Q(t2));  // open: load, up, count, D
  Comparator #(.width(4)) comparator_1 (.a(t2), .b(4'b0011), .eq(TimeOut));  // open: gt, lt

  // Notes on the sheet:
  //   3 min
endmodule

// s
module seconds_counter (
  input  game_end,
  input  reset,
  input  set,
  output asec,
  output [3:0] s
);

  wire clk, hz64, or_1_out, or_2_out, s_r_ff_1_q, start;

  Clock clock_1 (.out(clk));
  or or_1 (or_1_out, asec, reset);
  Counter #(.max('h1b), .width(6)) counter_1 (
    .clr(or_2_out), .count(start), .clk(clk), .carry(hz64));  // open: load, up, D, Q
  or or_2 (or_2_out, hz64, reset);
  Counter #(.max('h9), .width(4)) counter_2 (
    .clr(or_1_out), .clk(hz64), .carry(asec), .Q(s));  // open: load, up, count, D
  S_R_Flip_Flop s_r_ff_1 (.S(set), .R(reset), .clk(clk), .Q(s_r_ff_1_q));  // open: reset, Qn, preset
  and and_1 (start, ~game_end, s_r_ff_1_q);  // AND_Gate
endmodule

module buttons (
  input  check,
  input  b0,
  input  b1,
  input  b2,
  input  b3,
  input  b4,
  input  b5,
  input  b6,
  input  b7,
  input  b8,
  input  b9,
  input  [24:0] in_12,
  input  [24:0] in_13,
  input  [24:0] in_14,
  input  [24:0] in_15,
  input  [24:0] in_16,
  input  [24:0] in_17,
  input  [24:0] in_18,
  input  [24:0] in_19,
  input  [24:0] in_20,
  input  [24:0] in_21,
  output correct,
  output wrong
);

  wire bcheck, bx, c0, c1, clk, comparator_1_eq, reset, stop, undriven;
  wire [3:0] b_sel;
  wire [24:0] dx, register_1_q, register_2_q;

  Clock clock_1 (.out(clk));
  Priority_Encoder #(.select(4)) priority_encoder_1 (
    .in0(b0), .in1(b1), .in2(b2), .in3(b3), .in4(b4), .in5(b5), .in6(b6), .in7(b7), .in8(b8), .in9(b9),
    .out(b_sel));  // open: in10, in11, in12, in13, in14, in15, gs, en_out, en_in
  Counter #(.max('h3), .width(2)) counter_1 (
    .clr(reset), .count(undriven), .clk(bcheck), .carry(stop), .Q({c1, c0}));  // open: load, up, D
  Multiplexer #(.select(4), .width(25)) multiplexer_1 (
    .in0(in_12), .in1(in_13), .in2(in_14), .in3(in_15), .in4(in_16), .in5(in_17), .in6(in_18), .in7(in_19),
    .in8(in_20), .in9(in_21), .out(dx), .sel(b_sel));  // open: in10, in11, in12, in13, in14, in15
  ExactlyOne xor_1 (
    .out(bx), .in0(b0), .in1(b1), .in2(b2), .in3(b3), .in4(b4), .in5(b5), .in6(b6), .in7(b7), .in8(b8),
    .in9(b9));
  Register #(.trigger("falling"), .width(25)) register_1 (.D(dx), .en(c0), .clk(bx), .Q(register_1_q));  // open: clr
  Register #(.trigger("falling"), .width(25)) register_2 (.D(dx), .en(c1), .clk(bx), .Q(register_2_q));  // open: clr
  Counter #(.max('h1), .width(1)) counter_2 (
    .clr(reset), .count(stop), .clk(clk), .carry(reset));  // open: load, up, D, Q
  Comparator #(.width(25)) comparator_1 (.a(register_1_q), .b(register_2_q), .eq(comparator_1_eq));  // open: gt, lt
  ExactlyOne xor_2 (
    .out(bcheck), .in0(b0), .in1(b1), .in2(b2), .in3(b3), .in4(b4), .in5(b5), .in6(b6), .in7(b7), .in8(b8),
    .in9(b9), .in10(check));
  and and_1 (correct, comparator_1_eq, stop);
  and and_2 (wrong, ~correct, stop);  // AND_Gate

  // Other names for the same wires on the sheet: d0[24:0] = in_12; d1[24:0] = in_13; d2[24:0] = in_14;
  //   d3[24:0] = in_15; d4[24:0] = in_16; d5[24:0] = in_17; d6[24:0] = in_18; d7[24:0] = in_19; d8[24:0] = in_20;
  //   d9[24:0] = in_21
endmodule

// _
module single_display (
  input  [24:0] d,
  input  b,
  input  ep,
  input  miss,
  input  correct,
  input  in_6,
  output [4:0] out_7,
  output [4:0] out_8,
  output [4:0] out_9,
  output [4:0] out_10,
  output [4:0] out_11
);

  wire and_1_out, and_2_out, clk, comparator_1_eq, not_1_out, or_1_out, or_2_out, s_r_ff_2_q, s_r_ff_3_q,
       stop;
  wire [3:0] timer_1_t0;

  timer timer_1 (.set(ep), .reset(stop), .t0(timer_1_t0));  // open: in_3, TimeOut, t3, t2, t1
  Comparator #(.width(4)) comparator_1 (.a(timer_1_t0), .b(4'b0011), .eq(comparator_1_eq));  // open: gt, lt
  S_R_Flip_Flop s_r_ff_1 (.S(comparator_1_eq), .R(not_1_out), .clk(clk), .Q(stop));  // open: reset, Qn, preset
  not not_1 (not_1_out, ep);
  and and_1 (and_1_out, stop, ~or_2_out);  // AND_Gate
  S_R_Flip_Flop s_r_ff_2 (.Q(s_r_ff_2_q), .reset(or_1_out), .preset(b));  // open: S, R, clk, Qn
  or or_1 (or_1_out, miss, in_6);
  Multiplexer #(.width(25)) multiplexer_1 (
    .in0(d), .in1({25{1'b0}}), .out({out_11, out_10, out_9, out_8, out_7}), .sel(and_1_out));
  or or_2 (or_2_out, s_r_ff_2_q, s_r_ff_3_q);
  and and_2 (and_2_out, s_r_ff_2_q, correct);
  S_R_Flip_Flop s_r_ff_3 (.Q(s_r_ff_3_q), .reset(in_6), .preset(and_2_out));  // open: S, R, clk, Qn
  Clock clock_1 (.out(clk));

  // Other names for the same wires on the sheet: b_press = b; dx[24:0] = d; mistake = miss; reset = in_6
endmodule

// __
module single_display_mirrored (
  input  [24:0] in_1,
  input  in_2,
  input  in_3,
  input  in_4,
  input  correct,
  input  in_6,
  output [4:0] out_7,
  output [4:0] out_8,
  output [4:0] out_9,
  output [4:0] out_10,
  output [4:0] out_11
);

  wire and_1_out, and_2_out, clk, comparator_1_eq, not_1_out, or_1_out, or_2_out, s_r_ff_2_q, s_r_ff_3_q,
       stop;
  wire [3:0] timer_1_t0;

  timer timer_1 (.set(in_3), .reset(stop), .t0(timer_1_t0));  // open: in_3, TimeOut, t3, t2, t1
  Comparator #(.width(4)) comparator_1 (.a(timer_1_t0), .b(4'b0011), .eq(comparator_1_eq));  // open: gt, lt
  not not_1 (not_1_out, in_3);
  S_R_Flip_Flop s_r_ff_1 (.S(comparator_1_eq), .R(not_1_out), .clk(clk), .Q(stop));  // open: reset, Qn, preset
  and and_1 (and_1_out, stop, ~or_2_out);  // AND_Gate
  S_R_Flip_Flop s_r_ff_2 (.Q(s_r_ff_2_q), .reset(or_1_out), .preset(in_2));  // open: S, R, clk, Qn
  or or_1 (or_1_out, in_4, in_6);
  Multiplexer #(.width(25)) multiplexer_1 (
    .in0(in_1), .in1({25{1'b0}}), .out({out_7, out_8, out_9, out_10, out_11}), .sel(and_1_out));
  or or_2 (or_2_out, s_r_ff_2_q, s_r_ff_3_q);
  S_R_Flip_Flop s_r_ff_3 (.Q(s_r_ff_3_q), .reset(in_6), .preset(and_2_out));  // open: S, R, clk, Qn
  and and_2 (and_2_out, s_r_ff_2_q, correct);
  Clock clock_1 (.out(clk));

  // Other names for the same wires on the sheet: b_press = in_2; dx[24:0] = in_1; ep = in_3; mistake = in_4;
  //   reset = in_6
endmodule

module GameWon (
  input  Reset,
  input  GameWon
);

  wire clock_1_out, comparator_1_eq, comparator_1_lt, counter_1_carry, counter_2_carry, d_ff_1_q, or_1_out,
       or_2_out;
  wire [3:0] counter_2_q;
  wire [13:0] rom_1_data;

  Clock clock_1 (.out(clock_1_out));
  Counter #(.max('h7), .width(3)) counter_1 (
    .count(clock_1_out), .clk(clock_1_out), .carry(counter_1_carry));  // open: clr, load, up, D, Q
  D_Flip_Flop d_ff_1 (.D(GameWon), .clk(GameWon), .Q(d_ff_1_q), .reset(or_2_out));  // open: Qn, preset
  or or_1 (or_1_out, comparator_1_lt, d_ff_1_q);
  or or_2 (or_2_out, Reset, comparator_1_eq);
  Counter #(.max('hf), .width(4)) counter_2 (
    .clr(or_2_out), .count(or_1_out), .clk(counter_1_carry), .carry(counter_2_carry), .Q(counter_2_q));  // open: load, up, D
  ROM #(.addrWidth(4), .dataWidth(14)) rom_1 (.addr(counter_2_q), .data(rom_1_data));
  Comparator #(.width(14)) comparator_1 (
    .a(14'h1), .b(rom_1_data), .eq(comparator_1_eq), .lt(comparator_1_lt));  // open: gt
  // Buzzer #(.smooth_level(8), .smooth_width(8), .vol_width(8)) buzzer_1: pin names not known; wires that end beside it: rom_1_data, 8'h60, 1'b1

  // Notes on the sheet:
  //   contents of rom_1 (hex, n*v repeats v):
  //   0 190 190 200 190 190 200 200 258 258 190 258 3e8 3e8 4e8 1
endmodule

module GameLost (
  input  Reset,
  input  GameLost
);

  wire clock_1_out, comparator_1_eq, comparator_1_lt, counter_1_carry, counter_2_carry, d_ff_1_q, or_1_out,
       or_2_out;
  wire [3:0] counter_2_q;
  wire [13:0] rom_1_data;

  Clock clock_1 (.out(clock_1_out));
  Counter #(.max('h7), .width(3)) counter_1 (
    .count(clock_1_out), .clk(clock_1_out), .carry(counter_1_carry));  // open: clr, load, up, D, Q
  D_Flip_Flop d_ff_1 (.D(GameLost), .clk(GameLost), .Q(d_ff_1_q), .reset(or_2_out));  // open: Qn, preset
  or or_1 (or_1_out, comparator_1_lt, d_ff_1_q);
  or or_2 (or_2_out, Reset, comparator_1_eq);
  Counter #(.max('hf), .width(4)) counter_2 (
    .clr(or_2_out), .count(or_1_out), .clk(counter_1_carry), .carry(counter_2_carry), .Q(counter_2_q));  // open: load, up, D
  ROM #(.addrWidth(4), .dataWidth(14)) rom_1 (.addr(counter_2_q), .data(rom_1_data));
  Comparator #(.width(14)) comparator_1 (
    .a(14'h1), .b(rom_1_data), .eq(comparator_1_eq), .lt(comparator_1_lt));  // open: gt
  // Buzzer #(.smooth_level(8), .smooth_width(8), .vol_width(8)) buzzer_1: pin names not known; wires that end beside it: rom_1_data, 8'h60, 1'b1

  // Notes on the sheet:
  //   contents of rom_1 (hex, n*v repeats v):
  //   0 200 400 600 800 500 800 200 200 700 700 150 100 1
endmodule

module SoundSystem (
  input  Reset,
  input  SoundsON,
  input  Match,
  input  Wrong,
  input  Win,
  input  Lose
);

  wire and_1_out, and_2_out, and_3_out, and_4_out;

  and and_1 (and_1_out, SoundsON, Match);
  and and_2 (and_2_out, SoundsON, Wrong);
  and and_3 (and_3_out, SoundsON, Win);
  and and_4 (and_4_out, SoundsON, Lose);
  CorrectMatch correctmatch_1 (.Reset(Reset), .Match(and_1_out));
  WrongMatch wrongmatch_1 (.Reset(Reset), .Wrong(and_2_out));
  GameWon gamewon_1 (.Reset(Reset), .GameWon(and_3_out));
  GameLost gamelost_1 (.Reset(Reset), .GameLost(and_4_out));
endmodule

module CorrectMatch (
  input  Reset,
  input  Match
);

  wire clock_1_out, comparator_1_eq, comparator_1_lt, counter_1_carry, counter_2_carry, d_ff_1_q, or_1_out,
       or_2_out;
  wire [3:0] counter_2_q;
  wire [13:0] rom_1_data;

  Clock clock_1 (.out(clock_1_out));
  Counter #(.max('h7), .width(3)) counter_1 (
    .count(clock_1_out), .clk(clock_1_out), .carry(counter_1_carry));  // open: clr, load, up, D, Q
  D_Flip_Flop d_ff_1 (.D(Match), .clk(Match), .Q(d_ff_1_q), .reset(or_2_out));  // open: Qn, preset
  or or_1 (or_1_out, comparator_1_lt, d_ff_1_q);
  or or_2 (or_2_out, Reset, comparator_1_eq);
  Counter #(.max('hf), .width(4)) counter_2 (
    .clr(or_2_out), .count(or_1_out), .clk(counter_1_carry), .carry(counter_2_carry), .Q(counter_2_q));  // open: load, up, D
  ROM #(.addrWidth(4), .dataWidth(14)) rom_1 (.addr(counter_2_q), .data(rom_1_data));
  Comparator #(.width(14)) comparator_1 (
    .a(14'h1), .b(rom_1_data), .eq(comparator_1_eq), .lt(comparator_1_lt));  // open: gt
  // Buzzer #(.smooth_level(8), .smooth_width(8), .vol_width(8)) buzzer_1: pin names not known; wires that end beside it: rom_1_data, 8'h60, 1'b1

  // Notes on the sheet:
  //   contents of rom_1 (hex, n*v repeats v):
  //   0 400 350 1 5*0 100
endmodule

module WrongMatch (
  input  Reset,
  input  Wrong
);

  wire clock_1_out, comparator_1_eq, comparator_1_lt, counter_1_carry, counter_2_carry, d_ff_1_q, or_1_out,
       or_2_out;
  wire [3:0] counter_2_q;
  wire [13:0] rom_1_data;

  Clock clock_1 (.out(clock_1_out));
  Counter #(.max('h7), .width(3)) counter_1 (
    .count(clock_1_out), .clk(clock_1_out), .carry(counter_1_carry));  // open: clr, load, up, D, Q
  D_Flip_Flop d_ff_1 (.D(Wrong), .clk(Wrong), .Q(d_ff_1_q), .reset(or_2_out));  // open: Qn, preset
  or or_1 (or_1_out, comparator_1_lt, d_ff_1_q);
  or or_2 (or_2_out, Reset, comparator_1_eq);
  Counter #(.max('hf), .width(4)) counter_2 (
    .clr(or_2_out), .count(or_1_out), .clk(counter_1_carry), .carry(counter_2_carry), .Q(counter_2_q));  // open: load, up, D
  ROM #(.addrWidth(4), .dataWidth(14)) rom_1 (.addr(counter_2_q), .data(rom_1_data));
  Comparator #(.width(14)) comparator_1 (
    .a(14'h1), .b(rom_1_data), .eq(comparator_1_eq), .lt(comparator_1_lt));  // open: gt
  // Buzzer #(.smooth_level(8), .smooth_width(8), .vol_width(8)) buzzer_1: pin names not known; wires that end beside it: rom_1_data, 8'h60, 1'b1

  // Notes on the sheet:
  //   contents of rom_1 (hex, n*v repeats v):
  //   0 100 800 800 100 800 1 0 0 100
endmodule
